// Logisim project Circuito 2.circ as structural Verilog: 1 circuit, main circuit main
module main (
  input  A,
  input  B,
  input  C,
  output out_4,
  output out_5
);

  wire and_1_out, and_2_out, and_3_out, and_4_out, and_5_out, and_6_out, not_1_out, not_2_out, not_3_out,
       not_4_out, not_5_out, not_6_out, not_7_out, not_8_out, not_9_out, not_10_out, not_11_out, not_12_out,
       not_13_out;

  not not_1 (not_1_out, A);
  not not_2 (not_2_out, B);
  not not_3 (not_3_out, C);
  not not_4 (not_4_out, A);
  not not_5 (not_5_out, B);
  not not_6 (not_6_out, A);
  not not_7 (not_7_out, C);
  not not_8 (not_8_out, B);
  not not_9 (not_9_out, C);
  not not_10 (not_10_out, B);
  not not_11 (not_11_out, C);
  not not_12 (not_12_out, B);
  not not_13 (not_13_out, C);
  and and_1 (and_1_out, not_1_out, not_2_out, not_3_out);
  and and_2 (and_2_out, not_4_out, not_5_out, C);
  and and_3 (and_3_out, not_6_out, B, not_7_out);
  and and_4 (and_4_out, A, not_8_out, not_9_out);
  and and_5 (and_5_out, A, not_10_out, C);
  and and_6 (and_6_out, A, B, not_11_out);
  or or_1 (out_5, not_12_out, not_13_out);
  or or_2 (out_4, and_1_out, and_2_out, and_3_out, and_4_out, and_5_out, and_6_out);
endmodule
